# Fritzing sketch servo (saved by Fritzing 0.9.9b)

parts:
  MCU2 = Raspberry Pi Zero  # not connected
  KY-1 = Keyes Relay [package=THT]
  L1 = Solenoid  # not connected
  VCC1 = Battery block 9V

nets:
  N1: KY-1.C, VCC1.-

custom parts:
  Keyes Relay: The Keyes 5V relay module is suitable for SCM development, home appliance control. It uses a 5V~12V TIL control signal which can control DC / AC signal.
